# Fritzing sketch Circuit (saved by Fritzing 0.9.3b)

parts:
  LED1 = LED - 5mm [color="Red (633nm)" package="5 mm [THT]"]
  R1 = Resistor [tolerance=±5% resistance=220 package=THT]
  LED2 = LED - 5mm [color="Green (560nm)" package="5 mm [THT]"]
  R2 = Resistor [tolerance=±5% resistance=220 package=THT]
  LED3 = LED - 5mm [color="Blue (430nm)" package="5 mm [THT]"]
  R3 = Resistor [tolerance=±5% resistance=220 package=THT]  # not connected
  Part1 = Adafruit Circuit Playground Express [part_number="Adafruit #3333"]

nets:
  N1: LED1.anode, Part1.D10_A3
  N2: R1.Pin_0, R2.Pin_0, Part1.GND
  N3: LED2.anode, Part1.D9_A2
  N4: LED3.anode, Part1.D6_A1

custom parts:
  Adafruit Circuit Playground Express: Circuit Playground Express is the next step towards a perfect introduction to electronics and programming. We've taken the original Circuit Playground Classic and made it even better! Not only did we pack even more sensors in, we also made it even easier to program. You can now start your journey with Microsoft MakeCode block-based or Javascript programming. Then, you can use the same board to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
