# Fritzing sketch Circuit (saved by Fritzing 0.9.3b)

parts:
  LED1 = LED - 5mm [color="Red (633nm)" package="5 mm [THT]"]
  LED2 = LED - 5mm [color="Green (560nm)" package="5 mm [THT]"]
  R1 = Resistor [tolerance=±5% resistance=220 package=THT]
  LED3 = LED - 5mm [color="Blue (430nm)" package="5 mm [THT]"]
  R2 = Resistor [tolerance=±5% resistance=220 package=THT]
  R3 = Resistor [tolerance=±5% resistance=220 package=THT]
  Raspberry_Pi_1 = Raspberry Pi 3 [part_number=RPI-3-V1.2]

nets:
  N1: LED1.anode, Raspberry_Pi_1.GPIO17
  N2: LED2.anode, Raspberry_Pi_1.GPIO27
  N3: R1.Pin_0, R2.Pin_0, R3.Pin_0, Raspberry_Pi_1.GND
  N4: LED3.anode, Raspberry_Pi_1.GPIO22
