# Fritzing sketch Circuit (saved by Fritzing 0.9.3b)

parts:
  LED1 = LED - 5mm [color="Red (633nm)" package="5 mm [THT]"]
  R1 = Resistor [tolerance=±5% resistance=220 package=THT]
  Micro_bit1 = Microbit
  LED2 = LED - 5mm [color="Yellow (595nm)" package="5 mm [THT]"]
  R2 = Resistor [tolerance=±5% resistance=220 package=THT]
  LED3 = LED - 5mm [color="Blue (430nm)" package="5 mm [THT]"]
  R3 = Resistor [tolerance=±5% resistance=220 package=THT]

nets:
  N1: LED1.anode, Micro_bit1.0
  N2: R1.Pin_0, Micro_bit1.GND, R2.Pin_0, R3.Pin_0
  N3: Micro_bit1.1, LED2.anode
  N4: Micro_bit1.2, LED3.anode

custom parts:
  Microbit: BBC Microbit Fritzing part
